// Logisim project LED_Matrix_Test.circ as structural Verilog: 6 circuits, main circuit LED_Matrix_32x64
module LED_Matrix_32x64 (
);

  wire button_1_out, button_2_out, dipswitch_1_p25, dipswitch_1_p27, dipswitch_1_p28, dipswitch_1_p30,
       dipswitch_2_p1, dipswitch_2_p2, dipswitch_3_p1, dipswitch_3_p2, dipswitch_3_p3, dipswitch_3_p4,
       switch_1_p2, undriven, undriven_2, undriven_3, undriven_4;
  wire [63:0] dipswitch_1_p1, dipswitch_1_p2, dipswitch_1_p3, dipswitch_1_p4, dipswitch_1_p5, dipswitch_1_p6,
       dipswitch_1_p7, dipswitch_1_p8, dipswitch_1_p9, dipswitch_1_p10, dipswitch_1_p11, dipswitch_1_p12,
       dipswitch_1_p13, dipswitch_1_p14, dipswitch_1_p15, dipswitch_1_p16, dipswitch_1_p17, dipswitch_1_p18,
       dipswitch_1_p19, dipswitch_1_p20, dipswitch_1_p21, dipswitch_1_p22, dipswitch_1_p23, dipswitch_1_p24,
       led_matrix_32x64_driver_1_q24, led_matrix_32x64_driver_1_q25, led_matrix_32x64_driver_1_q26,
       led_matrix_32x64_driver_1_q27, led_matrix_32x64_driver_1_q28, led_matrix_32x64_driver_1_q29,
       led_matrix_32x64_driver_1_q30, led_matrix_32x64_driver_1_q31;

  // DotMatrix #(.dotshape("clusterSegment"), .inputtype("row"), .matrixcols(64), .matrixrows(32)) dotmatrix_1: pin names not known
  // NoConnect on nothing
  // DipSwitch #(.number(4)) dipswitch_1: pin names not known; wires that end beside it: dipswitch_1_p1, dipswitch_1_p2, dipswitch_1_p3, dipswitch_1_p4, dipswitch_1_p5, dipswitch_1_p6, dipswitch_1_p7, dipswitch_1_p8, dipswitch_1_p9, dipswitch_1_p10, dipswitch_1_p11, dipswitch_1_p12, dipswitch_1_p13, dipswitch_1_p14, dipswitch_1_p15, dipswitch_1_p16, dipswitch_1_p17, dipswitch_1_p18, dipswitch_1_p19, dipswitch_1_p20, dipswitch_1_p21, dipswitch_1_p22, dipswitch_1_p23, dipswitch_1_p24, dipswitch_1_p25, dipswitch_1_p25, dipswitch_1_p27, dipswitch_1_p28, dipswitch_1_p28, dipswitch_1_p30, dipswitch_1_p30
  // NoConnect on undriven
  // NoConnect on undriven_2
  // NoConnect on undriven_3
  // NoConnect on undriven_4
  LED_Matrix_32x64_Driver led_matrix_32x64_driver_1 (
    .Q30(led_matrix_32x64_driver_1_q30), .Q31(led_matrix_32x64_driver_1_q31), .Q0(dipswitch_1_p1),
    .Q1(dipswitch_1_p2), .Q2(dipswitch_1_p3), .Q3(dipswitch_1_p4), .Q4(dipswitch_1_p5), .Q5(dipswitch_1_p6),
    .Q6(dipswitch_1_p7), .Q7(dipswitch_1_p8), .Q8(dipswitch_1_p9), .Q9(dipswitch_1_p10),
    .Q10(dipswitch_1_p11), .Q11(dipswitch_1_p12), .Q12(dipswitch_1_p13), .Q13(dipswitch_1_p14),
    .Q14(dipswitch_1_p15), .Q15(dipswitch_1_p16), .Q16(dipswitch_1_p17), .Q17(dipswitch_1_p18),
    .Q18(dipswitch_1_p19), .Q19(dipswitch_1_p20), .Q20(dipswitch_1_p21), .Q21(dipswitch_1_p22),
    .Q22(dipswitch_1_p23), .Q23(dipswitch_1_p24), .Q24(led_matrix_32x64_driver_1_q24),
    .Q25(led_matrix_32x64_driver_1_q25), .Q26(led_matrix_32x64_driver_1_q26),
    .Q27(led_matrix_32x64_driver_1_q27), .Q28(led_matrix_32x64_driver_1_q28),
    .Q29(led_matrix_32x64_driver_1_q29), .OE_NOT(switch_1_p2), .LAT(button_2_out), .A(dipswitch_3_p1),
    .B(dipswitch_3_p2), .C(dipswitch_3_p3), .D(dipswitch_3_p4), .G1(dipswitch_1_p27), .CLK(button_1_out),
    .G2(dipswitch_2_p1), .B1(undriven_2), .B2(undriven_4), .R1(undriven), .R2(undriven_3), .GND2(1'b0),
    .GND3(1'b0), .GND1(1'b0));
  // NoConnect on nothing
  // DipSwitch #(.number(4)) dipswitch_2: pin names not known; wires that end beside it: dipswitch_2_p1, dipswitch_2_p2, dipswitch_2_p2
  // DipSwitch #(.number(4)) dipswitch_3: pin names not known; wires that end beside it: dipswitch_3_p1, dipswitch_3_p2, dipswitch_3_p3, dipswitch_3_p4
  Button button_1 (.out(button_1_out));
  // Switch switch_1: pin names not known; wires that end beside it: 1'b0, switch_1_p2
  Button button_2 (.out(button_2_out));
  Pull_Resistor #(.pull(1)) pull_resistor_1 (.node(switch_1_p2));

  // Notes on the sheet:
  //   RGB1
  //   RGB2
  //   ABCD
  //   CLK
  //   LAT
  //   !OE
endmodule

module Simple_Shift_Register_64Bit (
  input  NOT_OE,
  input  CLK,
  input  LAT,
  input  DIN,
  output [63:0] DOUT64
);

  wire shift_register_2_p1, shift_register_2_p2, shift_register_2_p3, shift_register_2_p4,
       shift_register_2_p5, shift_register_2_p6, shift_register_2_p7, shift_register_2_p8,
       shift_register_2_p9, shift_register_2_p10, shift_register_2_p11, shift_register_2_p12;
  wire [63:0] shift_register_2_p28;

  // Shift_Register #(.length(64)) shift_register_1: pin names not known; wires that end beside it: CLK, DIN
  // Shift_Register #(.length(64)) shift_register_2: pin names not known; wires that end beside it: shift_register_2_p1, shift_register_2_p2, shift_register_2_p3, shift_register_2_p4, shift_register_2_p5, shift_register_2_p6, shift_register_2_p7, shift_register_2_p8, shift_register_2_p9, shift_register_2_p10, shift_register_2_p11, shift_register_2_p12, 1'b1, 1'b0, LAT, shift_register_2_p1, shift_register_2_p2, shift_register_2_p3, shift_register_2_p4, shift_register_2_p5, shift_register_2_p6, shift_register_2_p7, shift_register_2_p8, shift_register_2_p9, shift_register_2_p10, shift_register_2_p11, shift_register_2_p12, shift_register_2_p28[0], shift_register_2_p28[1], shift_register_2_p28[2], shift_register_2_p28[3], shift_register_2_p28[4], shift_register_2_p28[5], shift_register_2_p28[6], shift_register_2_p28[7], shift_register_2_p28[8], shift_register_2_p28[9], shift_register_2_p28[10], shift_register_2_p28[11]
  assign DOUT64 = NOT_OE ? shift_register_2_p28 : 64'bz;  // Controlled_Buffer controlled_buffer_1
endmodule

module LED_Matrix_32x64_Driver (
  input  R1,
  input  OE_NOT,
  input  GND1,
  input  R2,
  input  LAT,
  input  GND2,
  input  GND3,
  input  G1,
  input  G2,
  input  A,
  input  CLK,
  input  B1,
  input  B2,
  input  B,
  input  C,
  input  D,
  output [63:0] Q0,
  output [63:0] Q1,
  output [63:0] Q2,
  output [63:0] Q3,
  output [63:0] Q4,
  output [63:0] Q5,
  output [63:0] Q6,
  output [63:0] Q7,
  output [63:0] Q8,
  output [63:0] Q9,
  output [63:0] Q10,
  output [63:0] Q11,
  output [63:0] Q12,
  output [63:0] Q13,
  output [63:0] Q14,
  output [63:0] Q15,
  output [63:0] Q16,
  output [63:0] Q17,
  output [63:0] Q18,
  output [63:0] Q19,
  output [63:0] Q20,
  output [63:0] Q21,
  output [63:0] Q22,
  output [63:0] Q23,
  output [63:0] Q24,
  output [63:0] Q25,
  output [63:0] Q26,
  output [63:0] Q27,
  output [63:0] Q28,
  output [63:0] Q29,
  output [63:0] Q30,
  output [63:0] Q31
);

  wire not_1_out;
  wire [63:0] simple_shift_register_64bit_1_dout64, simple_shift_register_64bit_2_dout64;

  not not_1 (not_1_out, OE_NOT);
  Simple_Shift_Register_64Bit simple_shift_register_64bit_1 (
    .DOUT64(simple_shift_register_64bit_1_dout64), .CLK(CLK), .DIN(G1), .LAT(LAT), .NOT_OE(not_1_out));
  Demultiplexer #(.select(4), .tristate("true"), .width(64)) demultiplexer_1 (
    .out0(Q0), .out1(Q1), .out2(Q2), .out3(Q3), .out4(Q4), .out5(Q5), .out6(Q6), .out7(Q7), .out8(Q8),
    .out9(Q9), .out10(Q10), .out11(Q11), .out12(Q12), .out13(Q13), .out14(Q14), .out15(Q15),
    .in(simple_shift_register_64bit_1_dout64), .sel({D, C, B, A}));
  Simple_Shift_Register_64Bit simple_shift_register_64bit_2 (
    .DOUT64(simple_shift_register_64bit_2_dout64), .CLK(CLK), .DIN(G2), .LAT(LAT), .NOT_OE(not_1_out));
  Demultiplexer #(.select(4), .tristate("true"), .width(64)) demultiplexer_2 (
    .out0(Q16), .out1(Q17), .out2(Q18), .out3(Q19), .out4(Q20), .out5(Q21), .out6(Q22), .out7(Q23),
    .out8(Q24), .out9(Q25), .out10(Q26), .out11(Q27), .out12(Q28), .out13(Q29), .out14(Q30), .out15(Q31),
    .in(simple_shift_register_64bit_2_dout64), .sel({D, C, B, A}));
endmodule

module LED_Matrix_With_Memory (
  input  in_1,
  input  [7:0] ADDR,
  input  in_3,
  input  in_4,
  input  in_5,
  input  CLK,
  input  [7:0] D
);

  wire button_1_out, button_2_out, dipswitch_1_p25, dipswitch_1_p27, dipswitch_1_p28, dipswitch_1_p30,
       dipswitch_2_p1, dipswitch_2_p2, dipswitch_2_p4, dipswitch_3_p1, dipswitch_3_p2, dipswitch_3_p3,
       not_1_out, switch_1_p2, undriven, undriven_2, undriven_3, undriven_4, undriven_5, undriven_6,
       undriven_7;
  wire [7:0] ram_1_dout;
  wire [63:0] led_matrix_32x64_driver_1_q0, led_matrix_32x64_driver_1_q1, led_matrix_32x64_driver_1_q2,
       led_matrix_32x64_driver_1_q3, led_matrix_32x64_driver_1_q4, led_matrix_32x64_driver_1_q5,
       led_matrix_32x64_driver_1_q6, led_matrix_32x64_driver_1_q7, led_matrix_32x64_driver_1_q8,
       led_matrix_32x64_driver_1_q9, led_matrix_32x64_driver_1_q10, led_matrix_32x64_driver_1_q11,
       led_matrix_32x64_driver_1_q12, led_matrix_32x64_driver_1_q13, led_matrix_32x64_driver_1_q14,
       led_matrix_32x64_driver_1_q15, led_matrix_32x64_driver_1_q16, led_matrix_32x64_driver_1_q17,
       led_matrix_32x64_driver_1_q18, led_matrix_32x64_driver_1_q19, led_matrix_32x64_driver_1_q20,
       led_matrix_32x64_driver_1_q21, led_matrix_32x64_driver_1_q22, led_matrix_32x64_driver_1_q23,
       led_matrix_32x64_driver_1_q24, led_matrix_32x64_driver_1_q25, led_matrix_32x64_driver_1_q26,
       led_matrix_32x64_driver_1_q27, led_matrix_32x64_driver_1_q28, led_matrix_32x64_driver_1_q29,
       led_matrix_32x64_driver_1_q30, led_matrix_32x64_driver_1_q31;

  // DotMatrix #(.dotshape("clusterSegment"), .inputtype("row"), .matrixcols(64), .matrixrows(32)) dotmatrix_1: pin names not known
  RAM ram_1 (.addr(ADDR), .we(in_4), .oe(in_5), .clk(CLK), .din(D), .dout(ram_1_dout));
  not not_1 (not_1_out, CLK);
  // Shift_Register shift_register_1: pin names not known; wires that end beside it: in_1, in_5, in_3, not_1_out, 1'b0
  Shift_Register shift_register_2 ();  // open: shift, in, clk, out, load, clr, d0, q0, d1, q1, d2, q2, d3, q3, d4, q4, d5, q5, d6, q6, d7, q7
  // NoConnect on undriven
  // NoConnect on undriven_2
  // NoConnect on undriven_5
  // NoConnect on undriven_3
  // NoConnect on undriven_4
  // NoConnect on undriven_6
  LED_Matrix_32x64_Driver led_matrix_32x64_driver_1 (
    .Q30(led_matrix_32x64_driver_1_q30), .Q31(led_matrix_32x64_driver_1_q31),
    .Q0(led_matrix_32x64_driver_1_q0), .Q1(led_matrix_32x64_driver_1_q1), .Q2(led_matrix_32x64_driver_1_q2),
    .Q3(led_matrix_32x64_driver_1_q3), .Q4(led_matrix_32x64_driver_1_q4), .Q5(led_matrix_32x64_driver_1_q5),
    .Q6(led_matrix_32x64_driver_1_q6), .Q7(led_matrix_32x64_driver_1_q7), .Q8(led_matrix_32x64_driver_1_q8),
    .Q9(led_matrix_32x64_driver_1_q9), .Q10(led_matrix_32x64_driver_1_q10),
    .Q11(led_matrix_32x64_driver_1_q11), .Q12(led_matrix_32x64_driver_1_q12),
    .Q13(led_matrix_32x64_driver_1_q13), .Q14(led_matrix_32x64_driver_1_q14),
    .Q15(led_matrix_32x64_driver_1_q15), .Q16(led_matrix_32x64_driver_1_q16),
    .Q17(led_matrix_32x64_driver_1_q17), .Q18(led_matrix_32x64_driver_1_q18),
    .Q19(led_matrix_32x64_driver_1_q19), .Q20(led_matrix_32x64_driver_1_q20),
    .Q21(led_matrix_32x64_driver_1_q21), .Q22(led_matrix_32x64_driver_1_q22),
    .Q23(led_matrix_32x64_driver_1_q23), .Q24(led_matrix_32x64_driver_1_q24),
    .Q25(led_matrix_32x64_driver_1_q25), .Q26(led_matrix_32x64_driver_1_q26),
    .Q27(led_matrix_32x64_driver_1_q27), .Q28(led_matrix_32x64_driver_1_q28),
    .Q29(led_matrix_32x64_driver_1_q29), .OE_NOT(switch_1_p2), .LAT(button_2_out), .A(dipswitch_2_p4),
    .B(dipswitch_3_p1), .C(dipswitch_3_p2), .D(dipswitch_3_p3), .G1(dipswitch_1_p27), .CLK(button_1_out),
    .G2(dipswitch_2_p1), .B1(undriven_2), .B2(undriven_4), .R1(undriven), .R2(undriven_3), .GND2(undriven_6),
    .GND3(undriven_7), .GND1(undriven_5));
  // NoConnect on undriven_7
  // NoConnect on nothing
  // DipSwitch #(.number(4)) dipswitch_1: pin names not known; wires that end beside it: led_matrix_32x64_driver_1_q0, led_matrix_32x64_driver_1_q1, led_matrix_32x64_driver_1_q2, led_matrix_32x64_driver_1_q3, led_matrix_32x64_driver_1_q4, led_matrix_32x64_driver_1_q5, led_matrix_32x64_driver_1_q6, led_matrix_32x64_driver_1_q7, led_matrix_32x64_driver_1_q8, led_matrix_32x64_driver_1_q9, led_matrix_32x64_driver_1_q10, led_matrix_32x64_driver_1_q11, led_matrix_32x64_driver_1_q12, led_matrix_32x64_driver_1_q13, led_matrix_32x64_driver_1_q14, led_matrix_32x64_driver_1_q15, led_matrix_32x64_driver_1_q16, led_matrix_32x64_driver_1_q17, led_matrix_32x64_driver_1_q18, led_matrix_32x64_driver_1_q19, led_matrix_32x64_driver_1_q20, led_matrix_32x64_driver_1_q21, led_matrix_32x64_driver_1_q22, led_matrix_32x64_driver_1_q23, dipswitch_1_p25, dipswitch_1_p25, dipswitch_1_p27, dipswitch_1_p28, dipswitch_1_p28, dipswitch_1_p30, dipswitch_1_p30
  Counter counter_1 ();  // open: load, D, count, Q, carry, up, clk, clr
  // NoConnect on nothing
  // DipSwitch #(.number(4)) dipswitch_2: pin names not known; wires that end beside it: dipswitch_2_p1, dipswitch_2_p2, dipswitch_2_p2, dipswitch_2_p4
  Button button_1 (.out(button_1_out));
  // DipSwitch #(.number(4)) dipswitch_3: pin names not known; wires that end beside it: dipswitch_3_p1, dipswitch_3_p2, dipswitch_3_p3
  Button button_2 (.out(button_2_out));
  // Switch switch_1: pin names not known; wires that end beside it: 1'b0, switch_1_p2
  Pull_Resistor #(.pull(1)) pull_resistor_1 (.node(switch_1_p2));

  // Notes on the sheet:
  //   RGB1
  //   RGB2
  //   ABCD
  //   CLK
  //   LAT
  //   !OE
endmodule

module Serial_RAM (
  input  [7:0] ADDR,
  input  CLK
);

  RAM ram_1 (.addr(ADDR));  // open: we, oe, clk, din, dout
endmodule

module Simple_Shift_Register_8Bit (
  input  NOT_OE,
  input  CLK,
  input  LAT,
  input  DIN,
  output [7:0] DOUT8,
  output out_6
);

  wire shift_register_2_p1, shift_register_2_p2, shift_register_2_p3, shift_register_2_p4,
       shift_register_2_p5, shift_register_2_p6, shift_register_2_p7, shift_register_2_p8;
  wire [7:0] shift_register_2_p21;

  // Shift_Register #(.length(9)) shift_register_1: pin names not known; wires that end beside it: CLK, DIN
  // Shift_Register shift_register_2: pin names not known; wires that end beside it: shift_register_2_p1, shift_register_2_p2, shift_register_2_p3, shift_register_2_p4, shift_register_2_p5, shift_register_2_p6, shift_register_2_p7, shift_register_2_p8, out_6, 1'b1, 1'b0, LAT, shift_register_2_p1, shift_register_2_p2, shift_register_2_p3, shift_register_2_p4, shift_register_2_p5, shift_register_2_p6, shift_register_2_p7, shift_register_2_p8, shift_register_2_p21[0], shift_register_2_p21[1], shift_register_2_p21[2], shift_register_2_p21[3], shift_register_2_p21[4], shift_register_2_p21[5], shift_register_2_p21[6], shift_register_2_p21[7]
  assign DOUT8 = NOT_OE ? shift_register_2_p21 : 8'bz;  // Controlled_Buffer controlled_buffer_1
endmodule
